# Fritzing sketch circuit_diagram (saved by Fritzing 0.9.3b)
breadboards: 2

parts:
  M1 = DC Motor
  M2 = DC Motor
  VCC1 = Battery
  Part3 = Adafruit Motor/Stepper/Servo Shield [part_number="Adafruit #1438"]
  Part4 = Breadboard Power Supply Board SMD
  esp1 = ESP32 DevKitc V4
  S1 = Square Pushbutton
  hc-sr1 = hc-sr04
  J1 = Basic Servo
  J2 = Basic Servo

nets:
  N1: M1.pin_1, Part3.M1B
  N2: M1.pin_2, Part3.M1A
  N3: M2.pin_1, Part3.M2A
  N4: M2.pin_2, Part3.M2B
  GND: VCC1.-, Part3.GND, Part4.GND, esp1.CMD, hc-sr1.GND, J1.gnd, J2.gnd
  N5: VCC1.+, Part3.VMOTOR, Part4.VIN
  N6: Part3.AD5/SCL, esp1.IO21
  N7: Part3.AD4/SDA, esp1.IO22
  VCC: Part4.VCC, S1.leg1, hc-sr1.VCC, J1.vcc, J2.vcc
  N8: esp1.IO4, J1.pulse
  N9: esp1.IO16, hc-sr1.Echo
  N10: esp1.IO17, J2.pulse
  N11: esp1.IO5, hc-sr1.Trig
  N12: esp1.5V, S1.leg0

notes:
  5V
  6-12V

custom parts:
  Adafruit Motor/Stepper/Servo Shield: The original Adafruit Motorshield kit is one of our most beloved kits, which is why we decided to make something even better. We have upgraded the shield kit to make the bestest, easiest way to drive DC and Stepper motors. This shield will make quick work of your next robotics project! We kept the ability to drive up to 4 DC motors or 2 stepper motors, but added many improvements: Instead of a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
  ESP32 DevKitc V4: ESP32-DevKitC board with ESP32-WROOM-32 module. ESP32-DevKitC V4 is a small-sized ESP32-based development board produced by Espressif. Most of the pins on the ESP module are broken out to the pin headers on the board. The pins D0, D1, D2, D3, CMD and CLK are used internally for communication between ESP32 and SPI flash memory. They are grouped on both sides near the USB connector. Avoid using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
